// Logisim project U21CS089_CO_Practical_Q1.circ as structural Verilog: 1 circuit, main circuit main
module main (
  input  in_1,
  input  Enable,
  input  in_3,
  output out_4
);

  wire clock_1_out;

  Clock clock_1 (.out(clock_1_out));
  Multiplexer multiplexer_1 (.in0(in_1), .in1(clock_1_out), .out(out_4), .sel(in_3), .en(Enable));

  // Notes on the sheet:
  //   Manual Input
  //   Clock
  //   Selecting in Manual OR Timer
endmodule
