// Logisim project U21CS089_CO_Practical_Q2.circ as structural Verilog: 1 circuit, main circuit main
module main (
  input  in_1,
  input  in_2,
  input  A0,
  input  A1,
  input  A2,
  input  A3,
  input  A4,
  input  A5,
  input  A6,
  input  A7,
  output _0,
  output B0,
  output B1,
  output B2,
  output B3,
  output B4,
  output B5,
  output DISCARD,
  output _0_2,
  output DISCARD_2
);

  wire and_2_out, and_3_out, and_4_out, and_6_out, and_7_out, and_8_out, and_9_out, and_10_out, and_11_out,
       and_12_out, and_13_out, and_14_out, and_15_out, and_16_out, and_17_out, and_18_out, and_19_out,
       and_20_out, and_21_out, and_22_out, and_23_out, and_24_out, or_3_out, or_4_out, xor_1_out, xor_2_out,
       xor_4_out, xor_6_out;

  and and_1 (_0, in_1, A0);
  and and_2 (and_2_out, in_1, A1);
  and and_3 (and_3_out, in_1, A2);
  and and_4 (and_4_out, in_1, A3);
  and and_5 (_0_2, in_1, A7);
  and and_6 (and_6_out, in_1, A6);
  and and_7 (and_7_out, in_1, A5);
  and and_8 (and_8_out, in_1, A4);
  and and_9 (and_9_out, in_2, A0);
  and and_10 (and_10_out, in_2, A1);
  and and_11 (and_11_out, in_2, A2);
  and and_12 (and_12_out, in_2, A7);
  and and_13 (and_13_out, in_2, A6);
  and and_14 (and_14_out, in_2, A5);
  xor xor_1 (xor_1_out, and_11_out, and_4_out);
  and and_15 (and_15_out, and_4_out, and_11_out);
  xor xor_2 (xor_2_out, and_14_out, and_8_out);
  and and_16 (and_16_out, and_8_out, and_14_out);
  xor xor_3 (B5, and_9_out, and_2_out);
  and and_17 (and_17_out, and_9_out, and_2_out);
  xor xor_4 (xor_4_out, and_10_out, and_3_out);
  and and_18 (and_18_out, and_10_out, and_3_out);
  xor xor_5 (B0, and_12_out, and_6_out);
  and and_19 (and_19_out, and_12_out, and_6_out);
  xor xor_6 (xor_6_out, and_13_out, and_7_out);
  and and_20 (and_20_out, and_13_out, and_7_out);
  xor xor_7 (B3, or_3_out, xor_1_out);
  and and_21 (and_21_out, or_3_out, xor_1_out);
  xor xor_8 (B2, or_4_out, xor_2_out);
  and and_22 (and_22_out, or_4_out, xor_2_out);
  xor xor_9 (B4, and_17_out, xor_4_out);
  and and_23 (and_23_out, and_17_out, xor_4_out);
  or or_1 (DISCARD, and_21_out, and_15_out);
  xor xor_10 (B1, and_19_out, xor_6_out);
  and and_24 (and_24_out, and_19_out, xor_6_out);
  or or_2 (DISCARD_2, and_22_out, and_16_out);
  or or_3 (or_3_out, and_23_out, and_18_out);
  or or_4 (or_4_out, and_24_out, and_20_out);

  // Notes on the sheet:
  //   C0
  //   C1
  //   C0A0
  //   C0A0
  //   C0A1 + C1A0
  //   C0A2 + C1A1
  //   C0A3 + C1A2
  //   C0A1 + C1A0
  //   C0A2 + C1A1
  //   C0A3 + C1A2
endmodule
