// Logisim project U21CS089-Assign5.circ as structural Verilog: 1 circuit, main circuit main
module main (
  input  A,
  input  B,
  input  in_3,
  input  A_2,
  input  B_2,
  input  A_3,
  input  B_3,
  input  [1:0] in_8,
  output out_9
);

  wire nand_1_out, nor_1_out, not_1_out, xor_1_out;

  xor xor_1 (xor_1_out, A, B);
  // AND_Gate and_1 has open pins: in0=B, in1=not_1_out, out=open
  not not_1 (not_1_out, A);
  nand nand_1 (nand_1_out, A_2, B_2);
  nor nor_1 (nor_1_out, A_3, B_3);
  Multiplexer #(.select(2)) multiplexer_1 (
    .in0(in_3), .in1(xor_1_out), .in2(nand_1_out), .in3(nor_1_out), .out(out_9), .sel(in_8));  // open: en

  // Notes on the sheet:
  //   NAND
  //   XOR
  //   Subratactor
  //   1-bit ALU
endmodule
