// Logisim project U21CS089-Assignment6.circ as structural Verilog: 1 circuit, main circuit main
module main (
  input  A0,
  input  A1,
  input  A2,
  input  in_4,
  input  in_5,
  input  B0,
  input  B1,
  input  B2,
  input  B3,
  input  in_10,
  output C0,
  output C1,
  output C2,
  output C3,
  output C4,
  output C5,
  output C6
);

  wire adder_1_cout, adder_2_cout, adder_2_out, adder_3_cout, adder_3_out, adder_4_cout, adder_4_out,
       adder_5_cout, adder_6_cout, adder_7_cout, and_2_out, and_3_out, and_4_out, and_5_out, and_6_out,
       and_7_out, and_8_out, and_9_out, and_10_out, and_11_out, and_12_out;

  and and_1 (C0, A0, A0, B0);
  and and_2 (and_2_out, A0, A0, B1);
  and and_3 (and_3_out, A0, B2);
  and and_4 (and_4_out, A0, B3);
  and and_5 (and_5_out, A1, A1, B0);
  and and_6 (and_6_out, A1, B1);
  and and_7 (and_7_out, A1, B2);
  and and_8 (and_8_out, A1, B3);
  Adder #(.width(1)) adder_1 (.a(and_5_out), .b(and_2_out), .out(C1), .cin(in_4), .cout(adder_1_cout));
  Adder #(.width(1)) adder_2 (.a(and_6_out), .b(and_3_out), .out(adder_2_out), .cin(adder_1_cout), .cout(adder_2_cout));
  Adder #(.width(1)) adder_3 (.a(and_7_out), .b(and_4_out), .out(adder_3_out), .cin(adder_2_cout), .cout(adder_3_cout));
  Adder #(.width(1)) adder_4 (.a(and_8_out), .b(in_10), .out(adder_4_out), .cin(adder_3_cout), .cout(adder_4_cout));
  and and_9 (and_9_out, A2, B0);
  and and_10 (and_10_out, A2, B1);
  and and_11 (and_11_out, A2, B2);
  and and_12 (and_12_out, A2, B3);
  Adder #(.width(1)) adder_5 (.a(and_9_out), .b(adder_2_out), .out(C2), .cin(in_5), .cout(adder_5_cout));
  Adder #(.width(1)) adder_6 (.a(and_10_out), .b(adder_3_out), .out(C3), .cin(adder_5_cout), .cout(adder_6_cout));
  Adder #(.width(1)) adder_7 (.a(and_11_out), .b(adder_4_out), .out(C4), .cin(adder_6_cout), .cout(adder_7_cout));
  Adder #(.width(1)) adder_8 (.a(and_12_out), .b(adder_4_cout), .out(C5), .cin(adder_7_cout), .cout(C6));

  // Notes on the sheet:
  //   A0B1
  //   A0B2
  //   A0B3
  //   A1B0
  //   A1B1
  //   A1B2
  //   A2B0
  //   A2B1
endmodule
